# Fritzing sketch 4wdcar (saved by Fritzing 0.9.4)
breadboards: 1

parts:
  BAT1 = 18650 battery holder [package=battery-18650-kit]
  BAT2 = 18650 battery holder [package=battery-18650-kit]
  BAT3 = 18650 battery holder [package=battery-18650-kit]
  Parça1 = Bluetooth HC-06  # not connected
  L298N1 = L298N DC motor driver  # not connected
  Parça2 = Arduino Nano (Rev3.0)  # not connected

nets:
  N1: BAT1.+, BAT2.-, BAT3.+
  N2: BAT1.-, BAT2.+, BAT3.-

custom parts:
  18650 battery holder: 18650 Battery Holder
  L298N DC motor driver: 2x DC motor driver with 78M05 positive voltage regulator (7..35 V) L298N: max 46 V, 2 A Set 5 V Enable jumper to enable 5 V regultor (needed for the L298N) and +5 V output at screw terminal or supply external +5 V at screw terminal Set ENA and/or ENB to +5 V to enable motor permanently or supply ENA and/or ENB with PWM signal IN1 and IN2 set rotation directory for motor A (OUT1/OUT2) IN2 and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
