# Fritzing sketch 4wdcarr (saved by Fritzing 0.9.4)
breadboards: 2

parts:
  BAT1 = 18650 battery holder [package=battery-18650-kit]
  BAT2 = 18650 battery holder [package=battery-18650-kit]
  BAT3 = 18650 battery holder [package=battery-18650-kit]
  L298N1 = L298N DC motor driver
  Parça2 = Arduino Nano (Rev3.0)
  M3 = DC Motor
  M4 = DC Motor
  M2 = DC Motor
  M1 = DC Motor
  J1 = Buzzer
  LED1 = smd LED [color="White (6500K)" package="0603 [SMD]"]
  LED2 = smd LED [color="White (6500K)" package="0603 [SMD]"]
  LED3 = smd LED [color="White (6500K)" package="0603 [SMD]"]
  LED4 = smd LED [color="White (6500K)" package="0603 [SMD]"]
  LED5 = smd LED [color="Red (635nm)" package="0603 [SMD]"]
  LED6 = smd LED [color="Red (635nm)" package="0603 [SMD]"]
  Parça3 = Bluetooth HC-06
  R1 = Resistor [tolerance=±5% resistance=1k package=THT]
  R2 = Resistor [tolerance=±5% resistance=1k package=THT]
  R3 = Resistor [tolerance=±5% resistance=1k package=THT]
  hc-sr1 = hc-sr04

nets:
  N1: BAT1.+, BAT2.-, BAT3.+, L298N1.12V
  N2: BAT1.-, BAT2.+, BAT3.-, L298N1.GND
  N3: L298N1.OUT1, M2.pin_1, M1.pin_1
  N4: L298N1.OUT2, M2.pin_2, M1.pin_2
  N5: L298N1.OUT3, M3.pin_1, M4.pin_1
  N6: L298N1.OUT4, M3.pin_2, M4.pin_2
  N7: L298N1.IN1, Parça2.D6
  N8: L298N1.IN2, Parça2.D10
  N9: L298N1.IN3, Parça2.D5
  N10: L298N1.IN4, Parça2.D9
  N11: Parça2.D1/TX, R2.Pin_0
  N12: Parça2.D0/RX, Parça3.TXD
  GND: Parça2.GND, J1.pin1, LED1.cathode, LED2.cathode, LED3.cathode, LED4.cathode, LED5.cathode, LED6.cathode, Parça3.GND, R1.Pin_1, hc-sr1.GND
  N13: Parça2.D2, LED3.anode, LED4.anode
  N14: Parça2.D3, LED5.anode, LED6.anode
  N15: Parça2.D7, hc-sr1.Trig
  N16: Parça2.D8, hc-sr1.Echo
  N17: Parça2.D11/MOSI, J1.pin2
  N18: Parça2.D12/MISO, LED1.anode, LED2.anode
  VCC: Parça2.5V, Parça3.VCC, hc-sr1.VCC
  N19: Parça3.RXD, R2.Pin_1, R3.Pin_0
  N20: R1.Pin_0, R3.Pin_1

custom parts:
  18650 battery holder: 18650 Battery Holder
  L298N DC motor driver: 2x DC motor driver with 78M05 positive voltage regulator (7..35 V) L298N: max 46 V, 2 A Set 5 V Enable jumper to enable 5 V regultor (needed for the L298N) and +5 V output at screw terminal or supply external +5 V at screw terminal Set ENA and/or ENB to +5 V to enable motor permanently or supply ENA and/or ENB with PWM signal IN1 and IN2 set rotation directory for motor A (OUT1/OUT2) IN2 and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
  Buzzer: Fixed frequency buzzer
